# Fritzing sketch wiring (saved by Fritzing 0.9.2b)
perfboards: 1

parts:
  Arduino1 = Arduino Uno (Rev3)
  R1 = Resistor [tolerance=±5% resistance=220 package=THT]
  WS2812_LED_strip = Neopixel Strip -- Black (30/m)
  Power_plug_5V_>5A = Power plug
  100-200_µF = Electrolytic Capacitor [capacitance=0.1nF package="100 mil [THT, electrolytic]"]
  J1 = male pin header, 7 pins [form="♂ (male)"]
  J2 = male pin header, 6 pins [form="♂ (male)"]

nets:
  N1: Arduino1.D12/MISO, R1.Pin_0, J2.pin2
  GND: Arduino1.GND, WS2812_LED_strip.GND, Power_plug_5V_>5A.GND, 100-200_µF.-, J1.pin5
  N2: R1.Pin_1, WS2812_LED_strip.Din
  +5V: WS2812_LED_strip.+5V, Power_plug_5V_>5A.VCC

notes:
  Do not use Arduino's Power plug

custom parts:
  Neopixel Strip -- Black (30/m): These NeoPixel strips have 30 digitally-addressable pixel LEDs per meter and are very affordable and are only 12.5 mm wide, 10 mm if you remove the strip from the casing.
