# Fritzing sketch wiring (saved by Fritzing 0.9.2b)
perfboards: 1

parts:
  Arduino1 = Arduino Uno (Rev3)
  Power_plug_5V_>5A = Power plug
  100-200_µF = Electrolytic Capacitor [capacitance=0.1nF package="100 mil [THT, electrolytic]"]
  J1 = male pin header, 7 pins [form="♂ (male)"]
  NEOPIXEL1 = Neopixel Strip -- Black (30/m)
  NEOPIXEL2 = Neopixel Strip -- Black (30/m)
  NEOPIXEL3 = Neopixel Strip -- Black (30/m)
  NEOPIXEL4 = Neopixel Strip -- Black (30/m)
  J2 = male pin header, 10 pins [form="♂ (male)"]
  Composant1 = MPR121 Breakout

nets:
  N1: Arduino1.D12/MISO, NEOPIXEL1.Din, J2.pin6
  GND: Arduino1.GND, 100-200_µF.-, J1.pin5, J2.pin4, Composant1.GND
  N2: Arduino1.A4/SDA, J2.pin2, Composant1.SDA
  N3: Arduino1.A5/SCL, J2.pin1, Composant1.SCL
  3V3: Arduino1.3V3, J1.pin3, Composant1.3.3V
  N4: Power_plug_5V_>5A.GND, NEOPIXEL1.GND#1
  N5: Power_plug_5V_>5A.VCC, NEOPIXEL1.+5V#3
  N6: NEOPIXEL1.+5V#4, NEOPIXEL2.+5V#3
  N7: NEOPIXEL1.Dout, NEOPIXEL2.Din
  N8: NEOPIXEL1.GND#6, NEOPIXEL2.GND#1
  N9: NEOPIXEL2.+5V#4, NEOPIXEL3.+5V#3
  N10: NEOPIXEL2.Dout, NEOPIXEL3.Din
  N11: NEOPIXEL2.GND#6, NEOPIXEL3.GND#1
  N12: NEOPIXEL3.+5V#4, NEOPIXEL4.+5V#3
  N13: NEOPIXEL3.Dout, NEOPIXEL4.Din
  N14: NEOPIXEL3.GND#6, NEOPIXEL4.GND#1

custom parts:
  Neopixel Strip -- Black (30/m): These NeoPixel strips have 30 digitally-addressable pixel LEDs per meter and are very affordable and are only 12.5 mm wide, 10 mm if you remove the strip from the casing.
